# Fritzing sketch so do mach (saved by Fritzing 0.9.2b)

parts:
  Part1 = Arduino Uno (Rev3)  # not connected
  Part2 = Arduino Ethernet Shield (Rev3)
  DHT1 = DHT11 Humitidy and Temperature Sensor

nets:
  N1: Part2.D2, DHT1.DATA
  5V: Part2.5V, DHT1.VDD
  GND: Part2.GND, DHT1.GND

custom parts:
  DHT11 Humitidy and Temperature Sensor: DHT11 Humidity and Temperature Sensor
